# Fritzing sketch Sketch (saved by Fritzing 1.0.6)
breadboards: 1

parts:
  Part1 = SRF05 Ultrasonic Rangefinder
  U2 = WS2812 RGB LED strip
  U3 = ESP32-38PinWide [part_number=ESP32-38PinWide]
  R1 = Resistor [tolerance=±5% power=0.25W resistance=1k package=THT]
  R2 = Resistor [tolerance=±5% power=0.25W resistance=2k package=THT]

nets:
  VCC: Part1.VCC, U2.VCC, U3.3.3
  N1: Part1.Trig, U3.GPIO27
  N2: Part1.Echo, R2.Pin_1
  GND: Part1.GND, U2.GND, U3.GND
  N3: U2.DIN, U3.GPIO33
  N4: U3.GPIO26, R1.Pin_0
  N5: R1.Pin_1, R2.Pin_0

custom parts:
  WS2812 RGB LED strip: WS2812 strip
  ESP32-38PinWide: Generic 38-Pin ESP32 with wide format (only access to one side of pins on a breadboard) based on Stephen Lilley's HiLetgo ESP-WROOM-32 ESP32 ESP-32S Development Board.
